# Fritzing sketch FC28_Sensor (saved by Fritzing 0.9.9b)
breadboards: 1

parts:
  LDR = Arduino Uno (Rev3)
  Componente1 = FC-28 Soil Hygrometer Module
  Componente2 = FC-28 Soil Hygrometer Module - Probe
  KF-1 = KF-301 Relay [package=THT]
  M1 = gear-motor

nets:
  N1: LDR.A4/SDA, Componente1.AO
  N2: LDR.D8, KF-1.signal
  5V: LDR.5V, Componente1.VCC, KF-1.power, KF-1.NO
  GND: LDR.GND, Componente1.GND, KF-1.ground, M1.pin_2
  N3: Componente1.POS, Componente2.POS
  N4: Componente1.NEG, Componente2.NEG
  N5: KF-1.C, M1.pin_1

notes:
  5V
  A4
  8

custom parts:
  FC-28 Soil Hygrometer Module: The FC-28 is a soil hygrometer module that uses the Texas Instruments LM393 comparator chip to provide an analog measurement of soil humidity. The digital output is high when soil moisture is over a certain threshold, as determined by adjusting the potentiometer.
  FC-28 Soil Hygrometer Module - Probe: The FC-28 is a soil hygrometer module that uses the Texas Instruments LM393 comparator chip to provide an analog measurement of soil humidity.
  KF-301 Relay: KF-301
