# Fritzing sketch LDR_Sensor (saved by Fritzing 0.9.9b)
breadboards: 1

parts:
  Componente1 = Arduino Uno (Rev3)
  LED1 = smd LED [color="Red (633nm)" package="0805 [SMD]"]
  R1 = Resistor [tolerance=±5% resistance=220 package="2010 [SMD]"]
  R2 = Photocell (LDR) [package=THT]
  R3 = Resistor [tolerance=±5% resistance=220 package="2010 [SMD]"]

nets:
  N1: Componente1.A0, R2.pin_0, R3.Pin_0
  N2: Componente1.D12/MISO, LED1.anode
  N3: Componente1.5V, R3.Pin_1
  N4: Componente1.GND, R1.Pin_0
  N5: LED1.cathode, R1.Pin_1

notes:
  A0
  13
  5V
