# Fritzing sketch PlantSenseFull (saved by Fritzing 0.9.9b)
breadboards: 1

parts:
  U2 = NodeMCU V1.0
  R1 = Photocell (LDR) [package=THT]
  R2 = Resistor [tolerance=±5% resistance=220 package="1206 [SMD]"]
  Componente2 = FC-28 Soil Hygrometer Module
  Componente3 = FC-28 Soil Hygrometer Module - Probe
  LED1 = LED - 3mm [color="Red (633nm)" current=0.030 package="3 mm [THT]"]
  R4 = Resistor [tolerance=±5% resistance=220 package="2010 [SMD]"]
  LED2 = LED - 3mm [color="Green (555nm)" current=0.030 package="3 mm [THT]"]
  R5 = Resistor [tolerance=±5% resistance=220 package="2010 [SMD]"]

nets:
  N1: U2.D1, LED2.anode
  N2: U2.D2, LED1.anode
  GND: U2.GND, R1.pin_1, Componente2.GND, R4.Pin_0, R5.Pin_0
  N3: U2.D7, Componente2.DO
  VIN: U2.Vin, R2.Pin_0, Componente2.VCC
  N4: U2.A0, R1.pin_0, R2.Pin_1
  N5: Componente2.POS, Componente3.POS
  N6: Componente2.NEG, Componente3.NEG
  N7: LED1.cathode, R4.Pin_1
  N8: LED2.cathode, R5.Pin_1

notes:
  Resistor 1K
  A0
  D7
  D1
  D2

custom parts:
  NodeMCU V1.0: ESP8266 based NodeMCU
  FC-28 Soil Hygrometer Module: The FC-28 is a soil hygrometer module that uses the Texas Instruments LM393 comparator chip to provide an analog measurement of soil humidity. The digital output is high when soil moisture is over a certain threshold, as determined by adjusting the potentiometer.
  FC-28 Soil Hygrometer Module - Probe: The FC-28 is a soil hygrometer module that uses the Texas Instruments LM393 comparator chip to provide an analog measurement of soil humidity.
